# Fritzing sketch Medidor de consumo de energia (saved by Fritzing 0.9.3b)
breadboards: 1

parts:
  Componente1 = Arduino Uno (Rev3)
  C1 = Electrolytic Capacitor [capacitance=1µF package="100 mil [THT, electrolytic]"]
  LCD1 = LCD screen
  U1 = POT [package=pot_alpha_rv16af-20]
  R1 = Resistor [tolerance=±5% resistance=100 package=THT]
  R2 = Resistor [tolerance=±5% resistance=100 package=THT]
  L1 = sct-013 [part_number=sct-013 package="4Ucon 08780 [THT]"]

nets:
  N1: Componente1.A1, L1.pin_0
  N2: Componente1.D11_PWM/MOSI, LCD1.E
  N3: Componente1.D12/MISO, LCD1.RS
  GND: Componente1.GND, C1.+, LCD1.VSS, LCD1.R/W, LCD1.LED-, U1.E, R2.Pin_1
  N4: Componente1.D2, LCD1.DB7
  N5: Componente1.D3_PWM, LCD1.DB6
  N6: Componente1.D4, LCD1.DB5
  N7: Componente1.D5_PWM, LCD1.DB4
  5V: Componente1.5V, LCD1.VDD, LCD1.LED+, U1.A, R1.Pin_0
  N8: C1.-, R1.Pin_1, R2.Pin_0, L1.pin_1
  N9: LCD1.V0, U1.S

custom parts:
  sct-013: sct-013 Current transformer. The pcb footprint is from the 3.5mm stereo jack (as the sensor comes with a 3.5 mm stero plug).

// code stored in the sketch: GS.ino

#include "EmonLib.h" 
#include <LiquidCrystal.h>
 
EnergyMonitor emon1;
LiquidCrystal lcd(12, 11, 5, 4, 3, 2);
 
//Tensao da rede eletrica
int rede = 110.0;
 
//Pino do sensor SCT
int pino_sct = 1;
 
void setup() 
{
  lcd.begin(16, 2);
  lcd.clear();
  Serial.begin(9600);   
  //Pino, calibracao - Cur Const= Ratio/BurdenR. 1800/62 = 29. 
  emon1.current(pino_sct, 29);
  //Informacoes iniciais display
  lcd.setCursor(0,0);
  lcd.print("Corr.(A):");
  lcd.setCursor(0,1);
  lcd.print("Pot. (W):");
} 
  
void loop() 
{ 
  //Calcula a corrente  
  double Irms = emon1.calcIrms(1480);
  //Mostra o valor da corrente
  Serial.print("Corrente : ");
  Serial.print(Irms); // Irms
  lcd.setCursor(10,0);
  lcd.print(Irms);
   
  //Calcula e mostra o valor da potencia
  Serial.print(" Potencia : ");
  Serial.println(Irms*rede);
  lcd.setCursor(10,1);
  lcd.print("      ");
  lcd.setCursor(10,1);
  lcd.print(Irms*rede,1);
   
  delay(1000);
}
